# Fritzing sketch rp2040_schematic (saved by Fritzing 0.9.6b)

parts:
  Mod1 = Raspberry Pi Pico
  RE1 = Rotary Encoder [package=THT]
  S1 = Pushbutton [package="[THT]"]
  S2 = Pushbutton [package="[THT]"]
  Bauteil1 = OLED Monochrome 128x64 1.3 inch [part_number=938]
  R1 = Rotary Potentiometer (Small) [maximum_resistance=100kΩ package=THT]
  R2 = Rotary Potentiometer (Small) [maximum_resistance=100kΩ package=THT]
  R3 = Rotary Potentiometer (Small) [maximum_resistance=100kΩ package=THT]
  I2S_Interface = female pin header, 5 pins [form="♀ (female)"]
  12V_Power_Supply = Power Jack [package=power_jack_combo]
  Guitar_Input = AUDIO-JACK2 [package=audio-jack]
  R10 = Rotary Potentiometer (Small) [maximum_resistance=10kΩ package=THT]
  IC4 = Audio Codec Board for Guitar
  Output = AUDIO-JACK2 [package=audio-jack]
  R11 = Rotary Potentiometer (Small) [maximum_resistance=10kΩ package=THT]

nets:
  GND: Mod1.pin_3, Mod1.pin_18, Mod1.pin_23, Mod1.pin_33, Mod1.pin_42, RE1.EncoderPinC, S1.Pin_2, S2.Pin_1, S2.Pin_2, Bauteil1.GND, R1.leg1, R2.leg1, R3.leg1, 12V_Power_Supply.GND, Guitar_Input.SLEEVE, R10.leg1, IC4.gnd, Output.SLEEVE, R11.leg1
  N1: Mod1.pin_5, IC4.reset
  N2: Mod1.pin_6, IC4.sda
  N3: Mod1.pin_7, IC4.scl
  N4: Mod1.pin_9, RE1.EncoderPinA
  N5: Mod1.pin_10, RE1.EncoderPinB
  N6: Mod1.pin_11, I2S_Interface.pin5
  N7: Mod1.pin_12, I2S_Interface.pin3, IC4.sdin
  N8: Mod1.pin_14, I2S_Interface.pin4, IC4.lrclk
  N9: Mod1.pin_15, I2S_Interface.pin1, IC4.sclk
  N10: Mod1.pin_16, I2S_Interface.pin2, IC4.sdout
  N11: Mod1.pin_19, Bauteil1.DC_SA0
  N12: Mod1.pin_20, Bauteil1.RESET
  N13: Mod1.pin_24, Bauteil1.SCLK_SCK
  N14: Mod1.pin_25, Bauteil1.MOSI_SDA
  N15: Mod1.pin_26, S2.Pin_3, S2.Pin_4
  N16: Mod1.pin_27, Bauteil1.CS
  N17: Mod1.pin_29, S1.Pin_3
  N18: Mod1.pin_31, R1.wiper
  N19: Mod1.pin_32, R2.wiper
  N20: Mod1.pin_34, R3.wiper
  3.3V: Mod1.pin_36, Bauteil1.3.3V, R1.leg2, R2.leg2, R3.leg2
  N21: Mod1.pin_39, IC4.5V_Out
  N22: 12V_Power_Supply.PWR, IC4.12V_In
  N23: Guitar_Input.RING, IC4.ina
  N24: R10.wiper, IC4.vol._out
  N25: R10.leg2, IC4.vol._in
  N26: IC4.outa, R11.leg2
  N27: Output.RING, R11.wiper

notes:
  BCLK
  Data out
  Data in
  LRCLK
  MCLK

custom parts:
  Raspberry Pi Pico: Raspberry Pi Pico. Based around the RP2040 microcontroller the Pico is a low cost microcontroller device bringing Raspberry Pi quality, cost, and easy of use to the microcontroller space. Jan 2021, Split part in to two versions: tht (this one) and SMD. This one will drill holes for a .1 in header in pcb to allow plugging in the module as well as providing pads to solder the module to the top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
  OLED Monochrome 128x64 1.3 inch: These displays are small, only about 1.3" diagonal, but very readable due to the high contrast of an OLED display. This display is made of 128x64 individual white OLED pixels, each one is turned on or off by the controller chip. Because the display makes its own light, no backlight is required. This reduces the power required to run the OLED and is why the display has such high contrast; we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
  Audio Codec Board for Guitar: Audio Codec Board built audio a cs4270
